# Fritzing sketch ArduinoCircuitSketch (saved by Fritzing 0.9.3b)
breadboards: 1

parts:
  元件1 = Arduino Uno (Rev3)
  J1 = Piezo Speaker
  S1 = Pushbutton [package="[THT]"]
  S2 = Pushbutton [package="[THT]"]
  R1 = Resistor [tolerance=±5% resistance=220 package=THT]
  R2 = Resistor [tolerance=±5% resistance=220 package=THT]
  R3 = Rotary Potentiometer (Small) [maximum_resistance=100kΩ package=THT]
  R4 = Resistor [tolerance=±5% resistance=220 package=THT]
  LED1 = LED - 5mm [color="Red (633nm)" package="5 mm [THT]"]
  LED2 = LED - 5mm [color="Red (633nm)" package="5 mm [THT]"]
  R5 = Resistor [tolerance=±5% resistance=220 package=THT]
  R6 = Resistor [tolerance=±5% resistance=220 package=THT]

nets:
  N1: 元件1.A0, R3.wiper
  N2: 元件1.D10_PWM/SS, LED2.anode, R5.Pin_0, R5.Pin_1
  N3: 元件1.D11_PWM/MOSI, R4.Pin_0, R4.Pin_1, LED1.anode
  N4: 元件1.GND, J1.pin1, R1.Pin_0, R2.Pin_0, R3.leg2, LED2.cathode, R6.Pin_0
  N5: 元件1.D3_PWM, S1.Pin_3, S1.Pin_4, R1.Pin_1
  N6: 元件1.D4, S2.Pin_1, S2.Pin_2, R2.Pin_1
  N7: 元件1.D5_PWM, J1.pin2, R6.Pin_1
  N8: S1.Pin_1, S1.Pin_2, S2.Pin_3, S2.Pin_4, R3.leg1
